// Logisim project 4-bit Subtractor.circ as structural Verilog: 1 circuit, main circuit main
module main (
  input  A,
  input  B,
  input  Bin,
  input  A_2,
  input  B_2,
  input  A_3,
  input  B_3,
  input  A_4,
  input  B_4
);

  wire and_1_out, and_2_out, and_3_out, and_4_out, and_5_out, and_6_out, and_7_out, and_8_out, not_1_out,
       not_2_out, not_3_out, not_4_out, not_5_out, not_6_out, not_7_out, not_8_out, or_1_out, or_2_out,
       or_3_out, or_4_out, xor_1_out, xor_2_out, xor_3_out, xor_4_out, xor_5_out, xor_6_out, xor_7_out,
       xor_8_out;

  xor xor_1 (xor_1_out, A, B);
  xor xor_2 (xor_2_out, A_2, B_2);
  xor xor_3 (xor_3_out, A_3, B_3);
  xor xor_4 (xor_4_out, A_4, B_4);
  not not_1 (not_1_out, xor_1_out);
  not not_2 (not_2_out, A);
  not not_3 (not_3_out, xor_2_out);
  not not_4 (not_4_out, A_2);
  not not_5 (not_5_out, xor_3_out);
  not not_6 (not_6_out, A_3);
  not not_7 (not_7_out, xor_4_out);
  not not_8 (not_8_out, A_4);
  and and_1 (and_1_out, not_1_out, Bin);
  and and_2 (and_2_out, not_2_out, B);
  and and_3 (and_3_out, not_5_out, or_2_out);
  and and_4 (and_4_out, not_6_out, B_3);
  and and_5 (and_5_out, not_7_out, or_3_out);
  and and_6 (and_6_out, not_8_out, B_4);
  xor xor_5 (xor_5_out, xor_1_out, Bin);
  xor xor_6 (xor_6_out, xor_2_out, or_1_out);
  and and_7 (and_7_out, not_4_out, B_2);
  xor xor_7 (xor_7_out, xor_4_out, or_3_out);
  or or_1 (or_1_out, and_1_out, and_2_out);
  and and_8 (and_8_out, not_3_out, or_1_out);
  LED led_1 (.in(xor_5_out));
  or or_2 (or_2_out, and_8_out, and_7_out);
  or or_3 (or_3_out, and_3_out, and_4_out);
  or or_4 (or_4_out, and_5_out, and_6_out);
  LED led_2 (.in(xor_6_out));
  LED led_3 (.in(xor_8_out));
  xor xor_8 (xor_8_out, xor_3_out, or_2_out);
  LED led_4 (.in(xor_7_out));
  LED led_5 (.in(or_4_out));

  // Notes on the sheet:
  //   Bin
  //   Bin
  //   Bin
  //   4-bit Subtractor
  //   D1
  //   Bout
  //   Bout
  //   Bout
  //   D2
  //   D3
  //   D4
  //   Bout
endmodule
