// Logisim project DeMultiplexer.circ as structural Verilog: 1 circuit, main circuit main
module main (
  input  A,
  input  B,
  input  D0
);

  wire and_1_out, and_2_out, and_3_out, and_4_out, not_1_out, not_2_out;

  not not_1 (not_1_out, A);
  not not_2 (not_2_out, B);
  and and_1 (and_1_out, not_1_out, not_2_out, D0);
  and and_2 (and_2_out, A, not_2_out, D0);
  LED led_1 (.in(and_1_out));
  LED led_2 (.in(and_3_out));
  and and_3 (and_3_out, not_1_out, B, D0);
  LED led_3 (.in(and_2_out));
  and and_4 (and_4_out, A, B, D0);
  LED led_4 (.in(and_4_out));

  // Notes on the sheet:
  //   DeMultiplexer
  //   Y0
  //   Y1
  //   Y2
  //   Y3
endmodule
