// Logisim project Full adder.circ as structural Verilog: 1 circuit, main circuit main
module main (
  input  A,
  input  B,
  input  Cin
);

  wire and_2_out, or_1_out, undriven, xor_1_out, xor_2_out;

  xor xor_1 (xor_1_out, A, B);
  // AND_Gate and_1 has open pins: in0=Cin, in1=Cin, in3=xor_1_out, out=open
  and and_2 (and_2_out, A, B);
  xor xor_2 (xor_2_out, xor_1_out, Cin);
  or or_1 (or_1_out, undriven, and_2_out);
  LED led_1 (.in(xor_2_out));
  LED led_2 (.in(or_1_out));

  // Notes on the sheet:
  //   S
  //   Cout
  //   SUM
  //   CARRY
endmodule
